// Logisim project cpu.circ as structural Verilog: 6 circuits, main circuit RegisterFile
module main (
);

  wire clock_1_out, control_1_aluop, control_1_alusrc, control_1_memread, control_1_memwrite,
       control_1_reg2loc, control_1_regwrite;
  wire [1:0] instruction_1_rd, instruction_1_rm, instruction_1_rn, multiplexer_1_out;
  wire [3:0] datamemory_1_out_6, datamemory_1_out_6_2, registerfile_1_regdata1, registerfile_1_regdata1_2,
       registerfile_1_regdata2, registerfile_1_regdata2_2;
  wire [4:0] instruction_1_imm5;
  wire [6:0] instruction_1_opcode;
  wire [7:0] adder_1_out, alu_1_out_6, bit_extender_1_out, PC_q;
  wire [15:0] ram_1_dout;

  Clock clock_1 (.out(clock_1_out));
  Register PC (.D(adder_1_out), .en(1'b1), .clk(clock_1_out), .Q(PC_q));  // open: clr
  Adder adder_1 (.a(8'h1), .b(PC_q), .out(adder_1_out));  // open: cin, cout
  RAM #(.dataWidth(16)) ram_1 (.addr(PC_q), .we(1'b0), .oe(1'b1), .clk(clock_1_out), .dout(ram_1_dout));  // open: din
  Instruction instruction_1 (
    .instructions(ram_1_dout), .Rd(instruction_1_rd), .Rn(instruction_1_rn), .imm5(instruction_1_imm5),
    .Rm(instruction_1_rm), .opcode(instruction_1_opcode));
  Control control_1 (
    .opcode(instruction_1_opcode), .MemRead(control_1_memread), .MemWrite(control_1_memwrite),
    .ALUsrc(control_1_alusrc), .ALUop(control_1_aluop), .RegWrite(control_1_regwrite),
    .Reg2Loc(control_1_reg2loc));  // open: MemToReg
  Multiplexer #(.width(2)) multiplexer_1 (
    .in0(instruction_1_rd), .in1(instruction_1_rm), .out(multiplexer_1_out), .sel(control_1_reg2loc));
  Hex_Digit_Display #(.decimalPoint("false")) hex_digit_display_1 (.value(registerfile_1_regdata1_2));
  Hex_Digit_Display Input1 (.value(registerfile_1_regdata1));  // open: dp
  assign bit_extender_1_out = {{3{instruction_1_imm5[4]}}, instruction_1_imm5};  // Bit_Extender bit_extender_1
  RegisterFile registerfile_1 (
    .Clock(clock_1_out), .WriteReg(instruction_1_rd), .ReadReg1(instruction_1_rn),
    .RegDataW({datamemory_1_out_6_2, datamemory_1_out_6}), .ReadReg2(multiplexer_1_out),
    .RegWrite(control_1_regwrite), .RegData1({registerfile_1_regdata1_2, registerfile_1_regdata1}),
    .RegData2({registerfile_1_regdata2_2, registerfile_1_regdata2}));
  Hex_Digit_Display hex_digit_display_2 (.value(registerfile_1_regdata2_2));  // open: dp
  Hex_Digit_Display Input2 (.value(registerfile_1_regdata2));  // open: dp
  Hex_Digit_Display hex_digit_display_3 (.value(datamemory_1_out_6_2));  // open: dp
  Hex_Digit_Display Outputt (.value(datamemory_1_out_6));  // open: dp
  ALU alu_1 (
    .RegData1({registerfile_1_regdata1_2, registerfile_1_regdata1}),
    .RegData2({registerfile_1_regdata2_2, registerfile_1_regdata2}), .imm(bit_extender_1_out),
    .ALUsrc(control_1_alusrc), .ALUop(control_1_aluop), .out_6(alu_1_out_6));
  DataMemory datamemory_1 (
    .ALUout(alu_1_out_6), .clock(clock_1_out), .MemWrite(control_1_memwrite),
    .RegData2({registerfile_1_regdata2_2, registerfile_1_regdata2}), .MemRead(control_1_memread),
    .out_6({datamemory_1_out_6_2, datamemory_1_out_6}));
endmodule

module RegisterFile (
  input  Clock,
  input  [1:0] WriteReg,
  input  [1:0] ReadReg1,
  input  [7:0] RegDataW,
  input  [1:0] ReadReg2,
  input  RegWrite,
  output [7:0] RegData1,
  output [7:0] RegData2
);

  wire and_1_out, and_2_out, and_3_out, and_4_out, decoder_1_out0, decoder_1_out1, decoder_1_out2,
       decoder_1_out3;
  wire [7:0] X0_q, X1_q, X2_q, X3_q;

  Decoder #(.select(2)) decoder_1 (
    .out0(decoder_1_out0), .out1(decoder_1_out1), .out2(decoder_1_out2), .out3(decoder_1_out3), .sel(WriteReg));  // open: en
  and and_1 (and_1_out, decoder_1_out0, RegWrite);
  and and_2 (and_2_out, decoder_1_out1, RegWrite);
  and and_3 (and_3_out, decoder_1_out2, RegWrite);
  and and_4 (and_4_out, decoder_1_out3, RegWrite);
  Register X0 (.D(RegDataW), .en(and_1_out), .clk(Clock), .Q(X0_q));  // open: clr
  Register X1 (.D(RegDataW), .en(and_2_out), .clk(Clock), .Q(X1_q));  // open: clr
  Register X2 (.D(RegDataW), .en(and_3_out), .clk(Clock), .Q(X2_q));  // open: clr
  Register X3 (.D(RegDataW), .en(and_4_out), .clk(Clock), .Q(X3_q));  // open: clr
  Multiplexer #(.select(2), .width(8)) multiplexer_1 (
    .in0(X0_q), .in1(X1_q), .in2(X2_q), .in3(X3_q), .out(RegData1), .sel(ReadReg1));
  Multiplexer #(.select(2), .width(8)) multiplexer_2 (
    .in0(X0_q), .in1(X1_q), .in2(X2_q), .in3(X3_q), .out(RegData2), .sel(ReadReg2));

  // Notes on the sheet:
  //   I pledge my honor that I have abided by the Stevens Honor System. Brayden Abo
endmodule

module Control (
  input  [6:0] opcode,
  output MemToReg,
  output MemRead,
  output MemWrite,
  output ALUsrc,
  output ALUop,
  output RegWrite,
  output Reg2Loc
);


  assign ALUop = opcode[4];
  assign ALUsrc = opcode[3];
  assign MemRead = opcode[1];
  assign MemToReg = opcode[0];
  assign MemWrite = opcode[2];
  assign Reg2Loc = opcode[6];
  assign RegWrite = opcode[5];

  // Notes on the sheet:
  //   Figure out what opcode bits relate to each control signal
endmodule

module Instruction (
  input  [15:0] instructions,
  output [1:0] Rd,
  output [1:0] Rn,
  output [4:0] imm5,
  output [1:0] Rm,
  output [6:0] opcode
);


  assign imm5 = instructions[8:4];
  assign opcode = instructions[15:9];
  assign Rd = instructions[1:0];
  assign Rm = instructions[8:7];
  assign Rn = instructions[3:2];
endmodule

module DataMemory (
  input  [7:0] ALUout,
  input  clock,
  input  MemWrite,
  input  [7:0] RegData2,
  input  MemRead,
  output [7:0] out_6
);

  wire [7:0] ram_1_dout;

  RAM ram_1 (.addr(ALUout), .we(MemWrite), .oe(1'b1), .clk(clock), .din(RegData2), .dout(ram_1_dout));
  Multiplexer #(.width(8)) multiplexer_1 (.in0(ALUout), .in1(ram_1_dout), .out(out_6), .sel(MemRead));
endmodule

module ALU (
  input  [7:0] RegData1,
  input  [7:0] RegData2,
  input  [7:0] imm,
  input  ALUsrc,
  input  ALUop,
  output [7:0] out_6
);

  wire adder_1_cout;
  wire [7:0] adder_1_out, multiplexer_1_out, subtractor_1_out;

  Multiplexer #(.width(8)) multiplexer_1 (.in0(RegData2), .in1(imm), .out(multiplexer_1_out), .sel(ALUsrc));
  Adder adder_1 (.a(RegData1), .b(multiplexer_1_out), .out(adder_1_out), .cout(adder_1_cout));  // open: cin
  Subtractor subtractor_1 (.a(RegData1), .b(multiplexer_1_out), .out(subtractor_1_out));  // open: bin, bout
  Multiplexer #(.width(8)) multiplexer_2 (.in0(adder_1_out), .in1(subtractor_1_out), .out(out_6), .sel(ALUop));
endmodule
